# Fritzing sketch cleaning_robot (saved by Fritzing 0.9.6b)
breadboards: 1

parts:
  L298N1 = L298N DC motor driver
  VCC1 = Battery block 9V
  M1 = DC Motor
  M2 = DC Motor
  J1 = STM32 Nucleo boards
  R1 = Resistor [tolerance=±5% resistance=220 package="1206 [SMD]"]
  J2 = Piezo Speaker
  M3 = DC Motor
  R2 = Resistor [tolerance=±5% resistance=220 package="1206 [SMD]"]
  Q1 = TRANSISTOR_PNP [package=to-92]
  S1 = Pushbutton [package="[THT]"]

nets:
  N1: L298N1.OUT1, M2.pin_2
  N2: L298N1.OUT2, M2.pin_1
  N3: L298N1.OUT3, M1.pin_2
  N4: L298N1.OUT4, M1.pin_1
  N5: L298N1.12V, R1.Pin_1
  N6: L298N1.GND, VCC1.-, J1.GND#1188, J1.PA10, J2.pin1, Q1.E, S1.Pin_3, S1.Pin_4
  N7: L298N1.5V, J1.E5V
  N8: L298N1.ENA, J1.A0
  N9: L298N1.ENB, J1.A1
  N10: L298N1.IN1, J1.PC0
  N11: L298N1.IN2, J1.PC1
  N12: L298N1.IN3, J1.PC2
  N13: L298N1.IN4, J1.PC3
  N14: VCC1.+, R1.Pin_0
  N15: J1.PA12, J2.pin2
  N16: J1.PA11, Q1.B
  N17: J1.IDD_01, J1.IDD_02
  N18: J1.CN_01, J1.CN_02
  N19: J1.CN_03, J1.CN_04
  N20: J1.JP5_2, J1.JP5_03
  N21: J1.GND#880, J1.GND#881
  N22: J1.GND#1149, J1.GND#1150
  N23: J1.3V3, S1.Pin_1, S1.Pin_2
  N24: J1.5V, M3.pin_1
  N25: M3.pin_2, R2.Pin_1
  N26: R2.Pin_0, Q1.C

notes:
  10 Ohm -> 11.8V
  vacuum
  10 Ohm

custom parts:
  L298N DC motor driver: 2x DC motor driver with 78M05 positive voltage regulator (7..35 V) L298N: max 46 V, 2 A Set 5 V Enable jumper to enable 5 V regultor (needed for the L298N) and +5 V output at screw terminal or supply external +5 V at screw terminal Set ENA and/or ENB to +5 V to enable motor permanently or supply ENA and/or ENB with PWM signal IN1 and IN2 set rotation directory for motor A (OUT1/OUT2) IN2 and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
