# Fritzing sketch cleaning_robot_v2 (saved by Fritzing 0.9.6b)
breadboards: 1

parts:
  J1 = STM32 Nucleo boards
  M4 = fc-51 [package=THT]
  LCD1 = LCD screen
  J4 = Buzzer
  R3 = Resistor [tolerance=±5% resistance=220 package="0402 [SMD]"]
  R4 = Rotary Potentiometer (Small) [maximum_resistance=100kΩ package=THT]
  LED1 = LED - 5mm [color="Red (633nm)" current=0.030 package="5 mm [THT]"]
  R5 = Resistor [tolerance=±5% resistance=220 package="0402 [SMD]"]
  LED2 = LED - 5mm [color="Red (633nm)" current=0.030 package="5 mm [THT]"]
  LED3 = LED - 5mm [color="Red (633nm)" current=0.030 package="5 mm [THT]"]
  LED4 = LED - 5mm [color="Red (633nm)" current=0.030 package="5 mm [THT]"]
  LED5 = LED - 5mm [color="Red (633nm)" current=0.030 package="5 mm [THT]"]
  R6 = Resistor [tolerance=±5% resistance=220 package="0402 [SMD]"]
  R7 = Resistor [tolerance=±5% resistance=220 package="0402 [SMD]"]
  R8 = Resistor [tolerance=±5% resistance=220 package="0402 [SMD]"]
  R9 = Resistor [tolerance=±5% resistance=220 package="0402 [SMD]"]

nets:
  N1: J1.PA12, J4.pin2
  N2: J1.IDD_01, J1.IDD_02
  N3: J1.CN_01, J1.CN_02
  N4: J1.CN_03, J1.CN_04
  N5: J1.JP5_1, J1.JP5_2
  N6: J1.GND#880, J1.GND#881
  N7: J1.JP1_2, J1.JP1_1
  N8: J1.GND#1149, J1.GND#1150
  N9: J1.3V3, M4.pin3, R3.Pin_1, R4.leg2
  5V: J1.5V, LCD1.VDD
  N10: J1.GND#1189, M4.pin2, LCD1.VSS, LCD1.R/W, LCD1.LED-, J4.pin1, R4.leg1, R5.Pin_1, R6.Pin_1, R7.Pin_1, R8.Pin_0, R9.Pin_0
  N11: J1.PB8, LCD1.E
  N12: J1.PB9, LCD1.RS
  N13: J1.PB6, LCD1.DB6
  N14: J1.PA9, M4.pin1
  N15: J1.PB4, LCD1.DB4
  N16: J1.PB5, LCD1.DB5
  N17: J1.PA10, LED1.anode
  N18: J1.PC1, LED3.anode
  N19: J1.PC0, LED5.anode
  N20: J1.PB7, LCD1.DB7
  N21: J1.PC2, LED4.anode
  N22: J1.PC3, LED2.anode
  N23: LCD1.V0, R4.wiper
  N24: LCD1.LED+, R3.Pin_0
  N25: LED1.cathode, R5.Pin_0
  N26: LED2.cathode, R8.Pin_1
  N27: LED3.cathode, R6.Pin_0
  N28: LED4.cathode, R9.Pin_1
  N29: LED5.cathode, R7.Pin_0

notes:
  The resistors attached to the LEDs are of 1K Ohm
  The resistor attached to the LCD display is of 330 Ohm

custom parts:
  Buzzer: Fixed frequency buzzer
